// Logisim project dazuoye.circ as structural Verilog: 14 circuits, main circuit main
module main (
  input  reset,
  output [5:0] opcode,
  output [5:0] \function 
);

  wire ALU_zero, ALUSrc, clk, j, Mem2Reg, MemWrite, nPC_Sel, RegDst, RegWrite;
  wire [1:0] ALUOp, ExtOp;
  wire [4:0] multiplexer_1_out, PCAdd, rd, rs, rt, shamt;
  wire [15:0] imm;
  wire [31:0] ALU_s, DM_o, multiplexer_2_out, multiplexer_3_out, \n20074411_32位extender_1_out_3 ,
       n20074411_gpr_1_busa, n20074411_gpr_1_busb, n20074411_ifu_1_instruction;

  Multiplexer #(.select(1), .width(5), .disabled("Z"), .enable("false")) multiplexer_1 (
    .in0(rt), .in1(rd), .out(multiplexer_1_out), .sel(RegDst));
  Clock #(.highDuration(1), .lowDuration(1)) clock_1 (.out(clk));
  _20074411_GPR u_20074411_gpr_1 (
    .in_1(RegWrite), .rs(rs), .rt(rt), .busW(multiplexer_3_out), .clk(clk), .busa(n20074411_gpr_1_busa),
    .busb(n20074411_gpr_1_busb), .RW(multiplexer_1_out));
  \_20074411_32位Extender  \u_20074411_32位extender_1  (
    .imm16(imm), .ExtOp(ExtOp), .out_3(\n20074411_32位extender_1_out_3 ));
  _20074411_IFU u_20074411_ifu_1 (
    .np_sel(nPC_Sel), .zero(ALU_zero), .clk(clk), .reset(reset), .J(j),
    .instruction(n20074411_ifu_1_instruction), .PCaddress(PCAdd));
  Multiplexer #(.select(1), .width(32), .disabled("Z"), .enable("false")) multiplexer_2 (
    .in0(n20074411_gpr_1_busb), .in1(\n20074411_32位extender_1_out_3 ), .out(multiplexer_2_out), .sel(ALUSrc));
  // Probe on n20074411_ifu_1_instruction
  \_20074411_译码  \u_20074411_译码_1  (
    .\input (n20074411_ifu_1_instruction), .fuction(\function ), .shamt(shamt), .rd(rd), .imm(imm), .rt(rt),
    .rs(rs), .pocode(opcode));
  \_20074411_32位ALU  ALU (.A(n20074411_gpr_1_busa), .B(multiplexer_2_out), .opcode(ALUOp), .S(ALU_s), .zero(ALU_zero));
  _20074411_DM DM (.Addr(ALU_s), .busB(n20074411_gpr_1_busb), .clk(clk), .MemWr(MemWrite), .o(DM_o));
  Multiplexer #(.select(1), .width(32), .disabled("Z"), .enable("false")) multiplexer_3 (
    .in0(ALU_s), .in1(DM_o), .out(multiplexer_3_out), .sel(Mem2Reg));
  _20074411_Control Controller (
    .opcode(opcode), .\function (\function ), .j(j), .ExtOp(ExtOp), .ALUctr(ALUOp), .RegDst(RegDst),
    .ALUsrc(ALUSrc), .MentoReg(Mem2Reg), .RegWr(RegWrite), .MenWr(MemWrite), .nPC_sel(nPC_Sel));

  // Other names for the same wires on the sheet: fuction[5:0] = \function 
endmodule

module _20074411_CLA4 (
  input  Cin,
  input  [3:0] p,
  input  [3:0] g,
  output [2:0] cout,
  output pm,
  output gm
);

  wire and_1_out, and_2_out, and_3_out, and_4_out, and_5_out, and_6_out, and_7_out, and_8_out, and_9_out,
       nand_1_out, nor_1_out, nor_2_out, nor_3_out, nor_4_out;

  and and_1 (and_1_out, Cin, p[0]);
  and and_2 (and_2_out, g[0], p[1]);
  and and_3 (and_3_out, Cin, p[1], p[0]);
  and and_4 (and_4_out, p[2], g[1]);
  and and_5 (and_5_out, g[0], p[2], p[1]);
  and and_6 (and_6_out, Cin, p[1], p[2], p[0]);
  and and_7 (and_7_out, p[3], g[2]);
  and and_8 (and_8_out, p[3], p[2], g[1]);
  and and_9 (and_9_out, p[2], p[3], p[1], g[0]);
  nor nor_1 (nor_1_out, g[0], and_1_out);
  nor nor_2 (nor_2_out, g[1], and_2_out, and_3_out);
  nor nor_3 (nor_3_out, g[2], and_4_out, and_5_out, and_6_out);
  nor nor_4 (nor_4_out, g[3], and_7_out, and_8_out, and_9_out);
  not not_1 (cout[0], nor_1_out);
  not not_2 (cout[1], nor_2_out);
  not not_3 (cout[2], nor_3_out);
  not not_4 (pm, nand_1_out);
  nand nand_1 (nand_1_out, p[0], p[1], Cin, p[2], p[3]);
  not not_5 (gm, nor_4_out);
endmodule

module \_20074411_4位超前进位加法器  (
  input  cin,
  input  [3:0] A_4,
  input  [3:0] B_4,
  output [3:0] S,
  output c4,
  output GM,
  output PM
);

  wire not_1_out, not_2_out;
  wire [2:0] n20074411_cla4_1_cout;
  wire [3:0] and_1_out, xor_1_out;

  xor xor_1 (xor_1_out[0], A_4[0], B_4[0]);
  xor xor_2 (xor_1_out[1], A_4[1], B_4[1]);
  xor xor_3 (xor_1_out[2], B_4[2], A_4[2]);
  xor xor_4 (xor_1_out[3], A_4[3], B_4[3]);
  and and_1 (and_1_out[0], A_4[0], B_4[0]);
  and and_2 (and_1_out[1], A_4[1], B_4[1]);
  and and_3 (and_1_out[2], A_4[2], B_4[2]);
  and and_4 (and_1_out[3], A_4[3], B_4[3]);
  _20074411_CLA4 u_20074411_cla4_1 (
    .Cin(cin), .p(xor_1_out), .g(and_1_out), .pm(PM), .gm(GM), .cout(n20074411_cla4_1_cout));
  not not_1 (not_1_out, GM);
  not not_2 (not_2_out, PM);
  xor xor_5 (S[0], cin, xor_1_out[0]);
  xor xor_6 (S[1], xor_1_out[1], n20074411_cla4_1_cout[0]);
  xor xor_7 (S[2], xor_1_out[2], n20074411_cla4_1_cout[1]);
  xor xor_8 (S[3], xor_1_out[3], n20074411_cla4_1_cout[2]);
  nand nand_1 (c4, not_1_out, not_2_out);
endmodule

module \_20074411_16位超前进位加法器  (
  input  [15:0] A_16,
  input  [15:0] B_16,
  input  cin,
  output [15:0] S,
  output c16
);

  wire n20074411_cla4_1_gm, n20074411_cla4_1_pm, not_1_out, not_2_out;
  wire [2:0] n20074411_cla4_1_cout;
  wire [3:0] \n20074411_4位超前进位加法器_1_gm , \n20074411_4位超前进位加法器_1_pm ;

  \_20074411_4位超前进位加法器  \u_20074411_4位超前进位加法器_1  (
    .cin(cin), .S(S[3:0]), .GM(\n20074411_4位超前进位加法器_1_gm [0]), .PM(\n20074411_4位超前进位加法器_1_pm [0]),
    .B_4(B_16[3:0]), .A_4(A_16[3:0]));  // open: c4
  \_20074411_4位超前进位加法器  \u_20074411_4位超前进位加法器_2  (
    .cin(n20074411_cla4_1_cout[0]), .S(S[7:4]), .GM(\n20074411_4位超前进位加法器_1_gm [1]),
    .PM(\n20074411_4位超前进位加法器_1_pm [1]), .B_4(B_16[7:4]), .A_4(A_16[7:4]));  // open: c4
  \_20074411_4位超前进位加法器  \u_20074411_4位超前进位加法器_3  (
    .cin(n20074411_cla4_1_cout[1]), .S(S[11:8]), .GM(\n20074411_4位超前进位加法器_1_gm [2]),
    .PM(\n20074411_4位超前进位加法器_1_pm [2]), .B_4(B_16[11:8]), .A_4(A_16[11:8]));  // open: c4
  \_20074411_4位超前进位加法器  \u_20074411_4位超前进位加法器_4  (
    .cin(n20074411_cla4_1_cout[2]), .S(S[15:12]), .GM(\n20074411_4位超前进位加法器_1_gm [3]),
    .PM(\n20074411_4位超前进位加法器_1_pm [3]), .B_4(B_16[15:12]), .A_4(A_16[15:12]));  // open: c4
  _20074411_CLA4 u_20074411_cla4_1 (
    .Cin(cin), .p(\n20074411_4位超前进位加法器_1_pm ), .g(\n20074411_4位超前进位加法器_1_gm ), .pm(n20074411_cla4_1_pm),
    .gm(n20074411_cla4_1_gm), .cout(n20074411_cla4_1_cout));
  not not_1 (not_1_out, n20074411_cla4_1_pm);
  not not_2 (not_2_out, n20074411_cla4_1_gm);
  nand nand_1 (c16, not_1_out, not_2_out);
endmodule

module \_20074411_32位加法器  (
  input  [31:0] A,
  input  [31:0] B,
  input  cin,
  output [31:0] out_4,
  output C32
);

  wire \n20074411_16位超前进位加法器_1_c16 ;

  \_20074411_16位超前进位加法器  \u_20074411_16位超前进位加法器_1  (
    .A_16(A[15:0]), .B_16(B[15:0]), .cin(cin), .S(out_4[15:0]), .c16(\n20074411_16位超前进位加法器_1_c16 ));
  \_20074411_16位超前进位加法器  \u_20074411_16位超前进位加法器_2  (
    .A_16(A[31:16]), .B_16(B[31:16]), .cin(\n20074411_16位超前进位加法器_1_c16 ), .S(out_4[31:16]), .c16(C32));
endmodule

module \_20074411_32位减法器  (
  input  [31:0] A,
  input  [31:0] B,
  output [31:0] out_3
);

  wire [31:0] \n20074411_32位加法器_1_out_4 , not_1_out;

  assign not_1_out = ~B;  // NOT_Gate not_1, 32 bits wide
  \_20074411_32位加法器  \u_20074411_32位加法器_1  (
    .A(not_1_out), .B(32'h1), .out_4(\n20074411_32位加法器_1_out_4 ), .cin(1'b0));  // open: C32
  \_20074411_32位加法器  \u_20074411_32位加法器_2  (
    .A(A), .B(\n20074411_32位加法器_1_out_4 ), .out_4(out_3), .cin(1'b0));  // open: C32
endmodule

module \_20074411_32位或运算  (
  input  [31:0] A,
  input  [31:0] B,
  output [31:0] out_3
);

  assign out_3 = A | B;  // OR_Gate or_1, 32 bits wide
endmodule

module \_20074411_32位ALU  (
  input  [31:0] A,
  input  [31:0] B,
  input  [1:0] opcode,
  output [31:0] S,
  output zero
);

  wire [31:0] \n20074411_32位减法器_1_out_3 , \n20074411_32位加法器_1_out_4 , \n20074411_32位或运算_1_out_3 ;

  \_20074411_32位加法器  \u_20074411_32位加法器_1  (.A(A), .B(B), .out_4(\n20074411_32位加法器_1_out_4 ), .cin(1'b0));  // open: C32
  \_20074411_32位减法器  \u_20074411_32位减法器_1  (.A(A), .B(B), .out_3(\n20074411_32位减法器_1_out_3 ));
  \_20074411_32位或运算  \u_20074411_32位或运算_1  (.A(A), .B(B), .out_3(\n20074411_32位或运算_1_out_3 ));
  Multiplexer #(.select(2), .width(32), .disabled("Z"), .enable("false")) multiplexer_1 (
    .in0(\n20074411_32位加法器_1_out_4 ), .in1(\n20074411_32位减法器_1_out_3 ), .in2(\n20074411_32位或运算_1_out_3 ),
    .out(S), .sel(opcode));  // open: in3
  Comparator #(.width(32), .mode("twosComplement")) comparator_1 (.a(S), .b({32{1'b0}}), .eq(zero));  // open: gt, lt
endmodule

// IFU
module _20074411_IFU (
  input  np_sel,
  input  zero,
  input  clk,
  input  reset,
  input  J,
  output [4:0] PCaddress,
  output [31:0] instruction
);

  wire and_1_out;
  wire [29:5] PC_q;
  wire [31:0] bit_extender_1_out, multiplexer_1_out, multiplexer_2_out, \n20074411_32位加法器_1_out_4 ,
       \n20074411_32位加法器_2_out_4 ;

  assign bit_extender_1_out = {{16{instruction[15]}}, instruction[15:0]};  // Bit_Extender bit_extender_1
  \_20074411_32位加法器  \u_20074411_32位加法器_1  (
    .A({2'b00, PC_q, PCaddress}), .B(32'h1), .out_4(\n20074411_32位加法器_1_out_4 ), .cin(1'b0));  // open: C32
  \_20074411_32位加法器  \u_20074411_32位加法器_2  (
    .A(\n20074411_32位加法器_1_out_4 ), .B(bit_extender_1_out), .out_4(\n20074411_32位加法器_2_out_4 ), .cin(1'b0));  // open: C32
  Multiplexer #(.select(1), .width(32), .disabled("Z"), .enable("false")) multiplexer_1 (
    .in0(\n20074411_32位加法器_1_out_4 ), .in1(\n20074411_32位加法器_2_out_4 ), .out(multiplexer_1_out),
    .sel(and_1_out));
  Multiplexer #(.select(1), .width(32), .disabled("Z"), .enable("false")) multiplexer_2 (
    .in0(multiplexer_1_out), .in1({2'b00, PC_q[29:26], instruction[25:0]}), .out(multiplexer_2_out), .sel(J));
  and and_1 (and_1_out, np_sel, zero);
  Register #(.width(30), .trigger("rising"), .Select("low")) PC (
    .D(multiplexer_2_out[29:0]), .Q({PC_q, PCaddress}), .clk(clk), .clr(reset));  // open: en
  ROM #(.addrWidth(5), .dataWidth(32), .Select("low")) rom_1 (.addr(PCaddress), .data(instruction));
  // Probe on instruction

  // Notes on the sheet:
  //   20074411
  //   contents of rom_1 (hex, n*v repeats v):
  //   34030093 340600ae 664021 664823 12a0021 ac090010 8c0a0010 112a0002 3c0bcdcd 8000c0d 340befef
  //   3c094567 8000c07
endmodule

// Extender
module \_20074411_32位Extender  (
  input  [15:0] imm16,
  input  [1:0] ExtOp,
  output [31:0] out_3
);

  wire [31:0] bit_extender_1_out, bit_extender_2_out;

  assign bit_extender_1_out = {{16{1'b0}}, imm16};  // Bit_Extender bit_extender_1
  assign bit_extender_2_out = {{16{1'b1}}, imm16};  // Bit_Extender bit_extender_2
  Multiplexer #(.select(2), .width(32), .disabled("Z"), .enable("false")) multiplexer_1 (
    .in0(bit_extender_1_out), .in1(bit_extender_2_out), .in2({imm16, {16{1'b0}}}), .out(out_3), .sel(ExtOp));  // open: in3
endmodule

// 译码
module \_20074411_译码  (
  input  [31:0] \input ,
  output [5:0] fuction,
  output [4:0] shamt,
  output [4:0] rd,
  output [15:0] imm,
  output [4:0] rt,
  output [4:0] rs,
  output [5:0] pocode
);


  assign fuction = \input [5:0];
  assign imm = \input [15:0];
  assign pocode = \input [31:26];
  assign rd = \input [15:11];
  assign rs = \input [25:21];
  assign rt = \input [20:16];
  assign shamt = \input [10:6];
endmodule

module _20074411_Control (
  input  [5:0] opcode,
  input  [5:0] \function ,
  output j,
  output [1:0] ExtOp,
  output [1:0] ALUctr,
  output RegDst,
  output ALUsrc,
  output MentoReg,
  output RegWr,
  output MenWr,
  output nPC_sel
);

  wire addu_out, not_1_out, not_2_out, not_3_out, not_4_out, not_5_out, not_6_out, not_7_out, not_8_out,
       not_9_out, not_10_out, not_11_out, not_12_out, subu_out;

  not not_1 (not_1_out, opcode[0]);
  not not_2 (not_2_out, opcode[1]);
  not not_3 (not_3_out, opcode[2]);
  not not_4 (not_4_out, opcode[3]);
  not not_5 (not_5_out, opcode[4]);
  not not_6 (not_6_out, opcode[5]);
  not not_7 (not_7_out, \function [0]);
  not not_8 (not_8_out, \function [1]);
  not not_9 (not_9_out, \function [2]);
  not not_10 (not_10_out, \function [3]);
  not not_11 (not_11_out, \function [4]);
  not not_12 (not_12_out, \function [5]);
  and addu (addu_out, not_1_out, not_2_out, not_3_out, not_4_out, not_5_out, not_6_out, \function [0], not_8_out, not_9_out, not_10_out, not_11_out, \function [5]);
  and subu (subu_out, not_1_out, not_2_out, not_3_out, not_4_out, not_5_out, not_6_out, \function [0], \function [1], not_9_out, not_10_out, not_11_out, \function [5]);
  and ori (ALUctr[1], opcode[0], not_2_out, opcode[2], opcode[3], not_5_out, not_6_out);
  and lw (MentoReg, opcode[0], opcode[1], not_3_out, not_4_out, not_5_out, opcode[5]);
  and sw (MenWr, opcode[0], opcode[1], not_3_out, opcode[3], not_5_out, opcode[5]);
  and beq (nPC_sel, not_1_out, not_2_out, opcode[2], not_4_out, not_5_out, not_6_out);
  and lui (ExtOp[1], opcode[0], opcode[1], opcode[2], opcode[3], not_5_out, not_6_out);
  or or_1 (ExtOp[0], MentoReg, MenWr);
  and u_j (j, not_1_out, opcode[1], not_3_out, not_4_out, not_5_out, not_6_out);
  or or_2 (ALUctr[0], nPC_sel, subu_out);
  or or_3 (RegDst, addu_out, subu_out);
  or or_4 (ALUsrc, ALUctr[1], MentoReg, MenWr, ExtOp[1]);
  or or_5 (RegWr, addu_out, subu_out, ALUctr[1], MentoReg, ExtOp[1]);
endmodule

module _20074411_DM (
  input  [31:0] Addr,
  input  [31:0] busB,
  input  clk,
  input  MemWr,
  output [31:0] o
);

  RAM #(.addrWidth(5), .dataWidth(8), .bus("separate"), .Select("low")) ram_1 (
    .addr(Addr[4:0]), .din(busB[7:0]), .data(o[7:0]), .str(MemWr), .clk(clk));  // open: sel, ld, clr
  RAM #(.addrWidth(5), .dataWidth(8), .bus("separate"), .Select("low")) ram_2 (
    .addr(Addr[4:0]), .din(busB[15:8]), .data(o[15:8]), .str(MemWr), .clk(clk));  // open: sel, ld, clr
  RAM #(.addrWidth(5), .dataWidth(8), .bus("separate"), .Select("low")) ram_3 (
    .addr(Addr[4:0]), .din(busB[23:16]), .data(o[23:16]), .str(MemWr), .clk(clk));  // open: sel, ld, clr
  RAM #(.addrWidth(5), .dataWidth(8), .bus("separate"), .Select("low")) ram_4 (
    .addr(Addr[4:0]), .din(busB[31:24]), .data(o[31:24]), .str(MemWr), .clk(clk));  // open: sel, ld, clr
endmodule

module _20074411_GPR (
  input  in_1,
  input  [4:0] RW,
  input  [4:0] rs,
  input  [4:0] rt,
  input  [31:0] busW,
  input  clk,
  output [31:0] busa,
  output [31:0] busb
);

  wire _1, _2, _3, _4, _5, _6, _7, _8, _9, _10, _11, _12, _13, _14, _15, _16, _17, _18, _19, _20, _21, _22,
       _23, _24, _25, _26, _27, _28, _29, _30, _31, _32, decoder_1_out0, decoder_1_out1, decoder_1_out2,
       decoder_1_out3, decoder_1_out4, decoder_1_out5, decoder_1_out6, decoder_1_out7, decoder_1_out8,
       decoder_1_out9, decoder_1_out10, decoder_1_out11, decoder_1_out12, decoder_1_out14, decoder_1_out15,
       decoder_1_out16, decoder_1_out17, decoder_1_out18, decoder_1_out19, decoder_1_out20, decoder_1_out21,
       decoder_1_out22, decoder_1_out23, decoder_1_out24, decoder_1_out25, decoder_1_out26, decoder_1_out27,
       decoder_1_out28, decoder_1_out29, decoder_1_out30, decoder_1_out31;
  wire [31:0] PC_2_q, PC_3_q, PC_4_q, PC_5_q, PC_6_q, PC_7_q, PC_8_q, PC_9_q, PC_10_q, PC_11_q, PC_12_q,
       PC_13_q, PC_14_q, PC_15_q, PC_16_q, PC_17_q, PC_18_q, PC_19_q, PC_20_q, PC_q, register_1_q,
       register_2_q, register_3_q, register_4_q, register_5_q, register_6_q, register_7_q, register_8_q,
       register_9_q, register_10_q, register_11_q, register_12_q;

  Decoder #(.select(5), .tristate("false"), .disabled("Z"), .enable("false")) decoder_1 (
    .out0(decoder_1_out0), .out1(decoder_1_out1), .out2(decoder_1_out2), .out3(decoder_1_out3),
    .out4(decoder_1_out4), .out5(decoder_1_out5), .out6(decoder_1_out6), .out7(decoder_1_out7),
    .out8(decoder_1_out8), .out9(decoder_1_out9), .out10(decoder_1_out10), .out11(decoder_1_out11),
    .out12(decoder_1_out12), .out13(decoder_1_out12), .out14(decoder_1_out14), .out15(decoder_1_out15),
    .out16(decoder_1_out16), .out17(decoder_1_out17), .out18(decoder_1_out18), .out19(decoder_1_out19),
    .out20(decoder_1_out20), .out21(decoder_1_out21), .out22(decoder_1_out22), .out23(decoder_1_out23),
    .out24(decoder_1_out24), .out25(decoder_1_out25), .out26(decoder_1_out26), .out27(decoder_1_out27),
    .out28(decoder_1_out28), .out29(decoder_1_out29), .out30(decoder_1_out30), .out31(decoder_1_out31),
    .sel(RW));
  and and_1 (_1, decoder_1_out0, in_1);
  and and_2 (_2, decoder_1_out1, in_1);
  and and_3 (_3, decoder_1_out2, in_1);
  and and_4 (_4, decoder_1_out3, in_1);
  and and_5 (_5, decoder_1_out4, in_1);
  and and_6 (_6, decoder_1_out5, in_1);
  and and_7 (_7, decoder_1_out6, in_1);
  and and_8 (_8, decoder_1_out7, in_1);
  and and_9 (_9, decoder_1_out8, in_1);
  and and_10 (_10, decoder_1_out9, in_1);
  and and_11 (_11, decoder_1_out10, in_1);
  and and_12 (_12, decoder_1_out11, in_1);
  and and_13 (_13, decoder_1_out12, in_1);
  and and_14 (_14, decoder_1_out12, in_1);
  and and_15 (_15, decoder_1_out14, in_1);
  and and_16 (_16, decoder_1_out15, in_1);
  and and_17 (_17, decoder_1_out16, in_1);
  and and_18 (_18, decoder_1_out17, in_1);
  and and_19 (_19, decoder_1_out18, in_1);
  and and_20 (_20, decoder_1_out19, in_1);
  and and_21 (_21, decoder_1_out20, in_1);
  and and_22 (_22, decoder_1_out21, in_1);
  and and_23 (_23, decoder_1_out22, in_1);
  and and_24 (_24, decoder_1_out23, in_1);
  and and_25 (_25, decoder_1_out24, in_1);
  and and_26 (_26, decoder_1_out25, in_1);
  and and_27 (_27, decoder_1_out26, in_1);
  and and_28 (_28, decoder_1_out27, in_1);
  and and_29 (_29, decoder_1_out28, in_1);
  and and_30 (_30, decoder_1_out29, in_1);
  and and_31 (_31, decoder_1_out30, in_1);
  and and_32 (_32, decoder_1_out31, in_1);
  Register #(.width(32), .trigger("rising"), .Select("low")) register_1 (
    .D(busW), .en(_1), .Q(register_1_q), .clk(clk));  // open: clr
  Register #(.width(32), .trigger("rising"), .Select("low")) register_2 (
    .D(busW), .en(_5), .Q(register_2_q), .clk(clk));  // open: clr
  Register #(.width(32), .trigger("rising"), .Select("low")) register_3 (
    .D(busW), .en(_9), .Q(register_3_q), .clk(clk));  // open: clr
  Register #(.width(32), .trigger("rising"), .Select("low")) register_4 (
    .D(busW), .en(_13), .Q(register_4_q), .clk(clk));  // open: clr
  Register #(.width(32), .trigger("rising"), .Select("low")) register_5 (
    .D(busW), .en(_17), .Q(register_5_q), .clk(clk));  // open: clr
  Register #(.width(32), .trigger("rising"), .Select("low")) register_6 (
    .D(busW), .en(_21), .Q(register_6_q), .clk(clk));  // open: clr
  Register #(.width(32), .trigger("rising"), .Select("low")) register_7 (
    .D(busW), .en(_25), .Q(register_7_q), .clk(clk));  // open: clr
  Register #(.width(32), .trigger("rising"), .Select("low")) register_8 (
    .D(busW), .en(_29), .Q(register_8_q), .clk(clk));  // open: clr
  Register #(.width(32), .trigger("rising"), .Select("low")) PC (.D(busW), .en(_2), .Q(PC_q), .clk(clk));  // open: clr
  Register #(.width(32), .trigger("rising"), .Select("low")) PC_2 (
    .D(busW), .en(_6), .Q(PC_2_q), .clk(clk));  // open: clr
  Register #(.width(32), .trigger("rising"), .Select("low")) register_9 (
    .D(busW), .en(_10), .Q(register_9_q), .clk(clk));  // open: clr
  Register #(.width(32), .trigger("rising"), .Select("low")) PC_3 (
    .D(busW), .en(_14), .Q(PC_3_q), .clk(clk));  // open: clr
  Register #(.width(32), .trigger("rising"), .Select("low")) PC_4 (
    .D(busW), .en(_18), .Q(PC_4_q), .clk(clk));  // open: clr
  Register #(.width(32), .trigger("rising"), .Select("low")) PC_5 (
    .D(busW), .en(_22), .Q(PC_5_q), .clk(clk));  // open: clr
  Register #(.width(32), .trigger("rising"), .Select("low")) PC_6 (
    .D(busW), .en(_26), .Q(PC_6_q), .clk(clk));  // open: clr
  Register #(.width(32), .trigger("rising"), .Select("low")) PC_7 (
    .D(busW), .en(_30), .Q(PC_7_q), .clk(clk));  // open: clr
  Register #(.width(32), .trigger("rising"), .Select("low")) PC_8 (
    .D(busW), .en(_3), .Q(PC_8_q), .clk(clk));  // open: clr
  Register #(.width(32), .trigger("rising"), .Select("low")) register_10 (
    .D(busW), .en(_7), .Q(register_10_q), .clk(clk));  // open: clr
  Register #(.width(32), .trigger("rising"), .Select("low")) register_11 (
    .D(busW), .en(_11), .Q(register_11_q), .clk(clk));  // open: clr
  Register #(.width(32), .trigger("rising"), .Select("low")) PC_9 (
    .D(busW), .en(_15), .Q(PC_9_q), .clk(clk));  // open: clr
  Register #(.width(32), .trigger("rising"), .Select("low")) PC_10 (
    .D(busW), .en(_19), .Q(PC_10_q), .clk(clk));  // open: clr
  Register #(.width(32), .trigger("rising"), .Select("low")) PC_11 (
    .D(busW), .en(_23), .Q(PC_11_q), .clk(clk));  // open: clr
  Register #(.width(32), .trigger("rising"), .Select("low")) PC_12 (
    .D(busW), .en(_27), .Q(PC_12_q), .clk(clk));  // open: clr
  Register #(.width(32), .trigger("rising"), .Select("low")) PC_13 (
    .D(busW), .en(_31), .Q(PC_13_q), .clk(clk));  // open: clr
  Register #(.width(32), .trigger("rising"), .Select("low")) PC_14 (
    .D(busW), .en(_4), .Q(PC_14_q), .clk(clk));  // open: clr
  Register #(.width(32), .trigger("rising"), .Select("low")) PC_15 (
    .D(busW), .en(_8), .Q(PC_15_q), .clk(clk));  // open: clr
  Register #(.width(32), .trigger("rising"), .Select("low")) register_12 (
    .D(busW), .en(_12), .Q(register_12_q), .clk(clk));  // open: clr
  Register #(.width(32), .trigger("rising"), .Select("low")) PC_16 (
    .D(busW), .en(_16), .Q(PC_16_q), .clk(clk));  // open: clr
  Register #(.width(32), .trigger("rising"), .Select("low")) PC_17 (
    .D(busW), .en(_20), .Q(PC_17_q), .clk(clk));  // open: clr
  Register #(.width(32), .trigger("rising"), .Select("low")) PC_18 (
    .D(busW), .en(_24), .Q(PC_18_q), .clk(clk));  // open: clr
  Register #(.width(32), .trigger("rising"), .Select("low")) PC_19 (
    .D(busW), .en(_28), .Q(PC_19_q), .clk(clk));  // open: clr
  Register #(.width(32), .trigger("rising"), .Select("low")) PC_20 (
    .D(busW), .en(_32), .Q(PC_20_q), .clk(clk));  // open: clr
  Multiplexer #(.select(5), .width(32), .disabled("Z"), .enable("false")) multiplexer_1 (
    .in0(register_1_q), .in1(PC_q), .in2(PC_8_q), .in3(PC_14_q), .in4(register_2_q), .in5(PC_2_q),
    .in6(register_10_q), .in7(PC_15_q), .in8(register_3_q), .in9(register_9_q), .in10(register_11_q),
    .in11(register_12_q), .in12(register_4_q), .in13(PC_3_q), .in14(PC_9_q), .in15(PC_16_q),
    .in16(register_5_q), .in17(PC_4_q), .in18(PC_10_q), .in19(PC_17_q), .in20(register_6_q), .in21(PC_5_q),
    .in22(PC_11_q), .in23(PC_18_q), .in24(register_7_q), .in25(PC_6_q), .in26(PC_12_q), .in27(PC_19_q),
    .in28(register_8_q), .in29(PC_7_q), .in30(PC_13_q), .in31(PC_20_q), .out(busa), .sel(rs));
  Multiplexer #(.select(5), .width(32), .disabled("Z"), .enable("false")) multiplexer_2 (
    .in0(register_1_q), .in1(PC_q), .in2(PC_8_q), .in3(PC_14_q), .in4(register_2_q), .in5(PC_2_q),
    .in6(register_10_q), .in7(PC_15_q), .in8(register_3_q), .in9(register_9_q), .in10(register_11_q),
    .in11(register_12_q), .in12(register_4_q), .in13(PC_3_q), .in14(PC_9_q), .in15(PC_16_q),
    .in16(register_5_q), .in17(PC_4_q), .in18(PC_10_q), .in19(PC_17_q), .in20(register_6_q), .in21(PC_5_q),
    .in22(PC_11_q), .in23(PC_18_q), .in24(register_7_q), .in25(PC_6_q), .in26(PC_12_q), .in27(PC_19_q),
    .in28(register_8_q), .in29(PC_7_q), .in30(PC_13_q), .in31(PC_20_q), .out(busb), .sel(rt));

  // Other names for the same wires on the sheet: RegWrite = in_1
endmodule
